# Fritzing sketch envi_sensor (saved by Fritzing 0.9.3b)
breadboards: 1

parts:
  WEMOS = WeMos D1 Mini
  U10 = Hirose DF13 Series Header [part_number=DHT11 package=DF13C-3P-1.25V]
  10K = Resistor [tolerance=±5% resistance=10k package="2010 [SMD]"]
  LIGHT = Hirose DF13 Series Header [part_number=Light package=DF13C-2P-1.25V]
  R1 = Trimmer Potentiometer [maximum_resistance=10kΩ package=THT]

nets:
  N1: WEMOS.3V3, U10.1, 10K.Pin_1, LIGHT.1
  N2: WEMOS.A0, R1.wiper
  N3: WEMOS.D3, U10.3, 10K.Pin_0
  N4: WEMOS.G, U10.2, R1.leg1
  N5: LIGHT.2, R1.leg2
