# Fritzing sketch watering_array_v1 (saved by Fritzing 0.9.3b)
breadboards: 1

parts:
  WEMOS = WeMos D1 Mini
  R4 = Resistor [tolerance=±5% resistance=330 package=THT]
  V1 = DC Power [voltage=12V]
  P1 = Hirose DF13 Series Header [part_number=PUMP package=DF13C-2P-1.25V]
  D9 = Rectifier Diode [part_number=1N4001 package="300 mil [THT]"]
  D12 = Rectifier Diode [part_number=1N4001 package="300 mil [THT]"]
  TIP120 = TRANSISTOR_NPN [package=sot223]
  7805 = Voltage Regulator [package=to220-igo]
  100µF = Electrolytic Capacitor [package="2cm H-Type"]
  100µF_2 = Electrolytic Capacitor [package="2cm H-Type"]
  U10 = Hirose DF13 Series Header [part_number="SENSOR (digital)" package=DF13C-3P-1.25V]
  R6 = Trimmer Potentiometer [maximum_resistance=10kΩ package=THT]
  R5 = Trimmer Potentiometer [maximum_resistance=10kΩ package=THT]
  U11 = Hirose DF13 Series Header [part_number="SENSOR (analogl)" package=DF13C-3P-1.25V]
  U12 = Hirose DF13 Series Header [part_number="LED (green / red)" package=DF13C-3P-1.25V]
  R7 = Resistor [tolerance=±5% resistance=470 package=THT]
  R8 = Resistor [tolerance=±5% resistance=470 package=THT]
  U13 = Hirose DF13 Series Header [part_number="ON / OFF" package=DF13C-2P-1.25V]

nets:
  N1: WEMOS.3V3, U10.1, U11.1
  N2: WEMOS.5V, 7805.IN, 100µF_2.+
  N3: WEMOS.A0, R6.wiper
  N4: WEMOS.D3, R4.Pin_0
  N5: WEMOS.D6, R7.Pin_0
  N6: WEMOS.D7, R8.Pin_0
  N7: WEMOS.D8, R5.wiper
  N8: WEMOS.G, TIP120.E, 7805.GND, 100µF.-, 100µF_2.-, U10.2, R6.leg1, R5.leg1, U11.2, U12.2, U13.1
  N9: R4.Pin_1, TIP120.B
  N10: V1.V+, D12.anode
  N11: V1.V-, U13.2
  N12: P1.1, D9.anode, TIP120.C
  N13: P1.2, D9.cathode, D12.cathode, 7805.OUT, 100µF.+
  N14: U10.3, R5.leg2
  N15: R6.leg2, U11.3
  N16: U12.1, R8.Pin_1
  N17: U12.3, R7.Pin_1

// code stored in the sketch: Untitled.ino

